// Logisim project cpu.circ as structural Verilog
module cpu (
);

  wire [31:0] rom_1_data;

  \PC寄存器_32位寄存器  \pc寄存器_32位寄存器_1  ();  // open: D, en, clk, rst, Q
  ROM #(.dataWidth(32)) rom_1 (.data(rom_1_data));  // open: addr, sel
  \_32位寄存器  \u_32位寄存器_1  ();  // open: D, en, clk, rst, Q
  \_32位寄存器  \u_32位寄存器_2  (.D(rom_1_data));  // open: en, clk, rst, Q
  \寄存器堆  \u_寄存器堆_1  ();  // open: wa, wd, clk, rst, ra0, ra1, ra2, rd0, rd1, rd2
endmodule

module \PC寄存器_32位寄存器  (
  input  [31:0] D,
  input  en,
  input  clk,
  input  rst,
  output [31:0] Q
);

  Register #(.width(32)) register_1 (.D(D), .en(en), .Q(Q), .clk(clk), .clr(rst));
endmodule

module \指令存储器  (
  input  [31:0] in_1,
  output [31:0] out_2
);

  wire [15:0] \n32位转16位_1__16bits ;

  \_32位转16位  \u_32位转16位_1  (._32bits(in_1), ._16bits(\n32位转16位_1__16bits ));
  ROM #(.addrWidth(16), .dataWidth(32)) rom_1 (.addr(\n32位转16位_1__16bits ), .data(out_2));  // open: sel
endmodule

module \寄存器堆  (
  input  [4:0] wa,
  input  [31:0] wd,
  input  clk,
  input  rst,
  input  [4:0] ra0,
  input  [4:0] ra1,
  input  [4:0] ra2,
  output [31:0] rd0,
  output [31:0] rd1,
  output [31:0] rd2
);

  wire decoder_1_out0, decoder_1_out1, decoder_1_out2, decoder_1_out3, decoder_1_out4, decoder_1_out5,
       decoder_1_out6, decoder_1_out7, decoder_1_out8, decoder_1_out9, decoder_1_out10, decoder_1_out11,
       decoder_1_out12, decoder_1_out13, decoder_1_out14, decoder_1_out15, decoder_1_out16, decoder_1_out17,
       decoder_1_out18, decoder_1_out19, decoder_1_out20, decoder_1_out21, decoder_1_out22, decoder_1_out23,
       decoder_1_out24, decoder_1_out25, decoder_1_out26, decoder_1_out27, decoder_1_out28, decoder_1_out29,
       decoder_1_out30, decoder_1_out31;
  wire [31:0] \n32位寄存器_1_q , \n32位寄存器_2_q , \n32位寄存器_3_q , \n32位寄存器_4_q , \n32位寄存器_5_q , \n32位寄存器_6_q ,
       \n32位寄存器_7_q , \n32位寄存器_8_q , \n32位寄存器_9_q , \n32位寄存器_10_q , \n32位寄存器_11_q , \n32位寄存器_12_q ,
       \n32位寄存器_13_q , \n32位寄存器_14_q , \n32位寄存器_15_q , \n32位寄存器_16_q , \n32位寄存器_17_q , \n32位寄存器_18_q ,
       \n32位寄存器_19_q , \n32位寄存器_20_q , \n32位寄存器_21_q , \n32位寄存器_22_q , \n32位寄存器_23_q , \n32位寄存器_24_q ,
       \n32位寄存器_25_q , \n32位寄存器_26_q , \n32位寄存器_27_q , \n32位寄存器_28_q , \n32位寄存器_29_q , \n32位寄存器_30_q ,
       \n32位寄存器_31_q , \n32位寄存器_32_q ;

  Decoder #(.select(5)) decoder_1 (
    .out0(decoder_1_out0), .out1(decoder_1_out1), .out2(decoder_1_out2), .out3(decoder_1_out3),
    .out4(decoder_1_out4), .out5(decoder_1_out5), .out6(decoder_1_out6), .out7(decoder_1_out7),
    .out8(decoder_1_out8), .out9(decoder_1_out9), .out10(decoder_1_out10), .out11(decoder_1_out11),
    .out12(decoder_1_out12), .out13(decoder_1_out13), .out14(decoder_1_out14), .out15(decoder_1_out15),
    .out16(decoder_1_out16), .out17(decoder_1_out17), .out18(decoder_1_out18), .out19(decoder_1_out19),
    .out20(decoder_1_out20), .out21(decoder_1_out21), .out22(decoder_1_out22), .out23(decoder_1_out23),
    .out24(decoder_1_out24), .out25(decoder_1_out25), .out26(decoder_1_out26), .out27(decoder_1_out27),
    .out28(decoder_1_out28), .out29(decoder_1_out29), .out30(decoder_1_out30), .out31(decoder_1_out31),
    .sel(wa), .en(1'b1));
  \_32位寄存器  \u_32位寄存器_1  (.D(wd), .en(decoder_1_out0), .clk(clk), .rst(rst), .Q(\n32位寄存器_1_q ));
  \_32位寄存器  \u_32位寄存器_2  (.D(wd), .en(decoder_1_out4), .clk(clk), .rst(rst), .Q(\n32位寄存器_2_q ));
  \_32位寄存器  \u_32位寄存器_3  (.D(wd), .en(decoder_1_out8), .clk(clk), .rst(rst), .Q(\n32位寄存器_3_q ));
  \_32位寄存器  \u_32位寄存器_4  (.D(wd), .en(decoder_1_out12), .clk(clk), .rst(rst), .Q(\n32位寄存器_4_q ));
  \_32位寄存器  \u_32位寄存器_5  (.D(wd), .en(decoder_1_out16), .clk(clk), .rst(rst), .Q(\n32位寄存器_5_q ));
  \_32位寄存器  \u_32位寄存器_6  (.D(wd), .en(decoder_1_out20), .clk(clk), .rst(rst), .Q(\n32位寄存器_6_q ));
  \_32位寄存器  \u_32位寄存器_7  (.D(wd), .en(decoder_1_out24), .clk(clk), .rst(rst), .Q(\n32位寄存器_7_q ));
  \_32位寄存器  \u_32位寄存器_8  (.D(wd), .en(decoder_1_out28), .clk(clk), .rst(rst), .Q(\n32位寄存器_8_q ));
  \_32位寄存器  \u_32位寄存器_9  (.D(wd), .en(decoder_1_out1), .clk(clk), .rst(rst), .Q(\n32位寄存器_9_q ));
  \_32位寄存器  \u_32位寄存器_10  (.D(wd), .en(decoder_1_out5), .clk(clk), .rst(rst), .Q(\n32位寄存器_10_q ));
  \_32位寄存器  \u_32位寄存器_11  (.D(wd), .en(decoder_1_out9), .clk(clk), .rst(rst), .Q(\n32位寄存器_11_q ));
  \_32位寄存器  \u_32位寄存器_12  (.D(wd), .en(decoder_1_out13), .clk(clk), .rst(rst), .Q(\n32位寄存器_12_q ));
  \_32位寄存器  \u_32位寄存器_13  (.D(wd), .en(decoder_1_out17), .clk(clk), .rst(rst), .Q(\n32位寄存器_13_q ));
  \_32位寄存器  \u_32位寄存器_14  (.D(wd), .en(decoder_1_out21), .clk(clk), .rst(rst), .Q(\n32位寄存器_14_q ));
  \_32位寄存器  \u_32位寄存器_15  (.D(wd), .en(decoder_1_out25), .clk(clk), .rst(rst), .Q(\n32位寄存器_15_q ));
  \_32位寄存器  \u_32位寄存器_16  (.D(wd), .en(decoder_1_out29), .clk(clk), .rst(rst), .Q(\n32位寄存器_16_q ));
  \_32位寄存器  \u_32位寄存器_17  (.D(wd), .en(decoder_1_out2), .clk(clk), .rst(rst), .Q(\n32位寄存器_17_q ));
  \_32位寄存器  \u_32位寄存器_18  (.D(wd), .en(decoder_1_out6), .clk(clk), .rst(rst), .Q(\n32位寄存器_18_q ));
  \_32位寄存器  \u_32位寄存器_19  (.D(wd), .en(decoder_1_out10), .clk(clk), .rst(rst), .Q(\n32位寄存器_19_q ));
  \_32位寄存器  \u_32位寄存器_20  (.D(wd), .en(decoder_1_out14), .clk(clk), .rst(rst), .Q(\n32位寄存器_20_q ));
  \_32位寄存器  \u_32位寄存器_21  (.D(wd), .en(decoder_1_out18), .clk(clk), .rst(rst), .Q(\n32位寄存器_21_q ));
  \_32位寄存器  \u_32位寄存器_22  (.D(wd), .en(decoder_1_out22), .clk(clk), .rst(rst), .Q(\n32位寄存器_22_q ));
  \_32位寄存器  \u_32位寄存器_23  (.D(wd), .en(decoder_1_out26), .clk(clk), .rst(rst), .Q(\n32位寄存器_23_q ));
  \_32位寄存器  \u_32位寄存器_24  (.D(wd), .en(decoder_1_out30), .clk(clk), .rst(rst), .Q(\n32位寄存器_24_q ));
  \_32位寄存器  \u_32位寄存器_25  (.D(wd), .en(decoder_1_out3), .clk(clk), .rst(rst), .Q(\n32位寄存器_25_q ));
  \_32位寄存器  \u_32位寄存器_26  (.D(wd), .en(decoder_1_out7), .clk(clk), .rst(rst), .Q(\n32位寄存器_26_q ));
  \_32位寄存器  \u_32位寄存器_27  (.D(wd), .en(decoder_1_out11), .clk(clk), .rst(rst), .Q(\n32位寄存器_27_q ));
  \_32位寄存器  \u_32位寄存器_28  (.D(wd), .en(decoder_1_out15), .clk(clk), .rst(rst), .Q(\n32位寄存器_28_q ));
  \_32位寄存器  \u_32位寄存器_29  (.D(wd), .en(decoder_1_out19), .clk(clk), .rst(rst), .Q(\n32位寄存器_29_q ));
  \_32位寄存器  \u_32位寄存器_30  (.D(wd), .en(decoder_1_out23), .clk(clk), .rst(rst), .Q(\n32位寄存器_30_q ));
  \_32位寄存器  \u_32位寄存器_31  (.D(wd), .en(decoder_1_out27), .clk(clk), .rst(rst), .Q(\n32位寄存器_31_q ));
  \_32位寄存器  \u_32位寄存器_32  (.D(wd), .en(decoder_1_out31), .clk(clk), .rst(rst), .Q(\n32位寄存器_32_q ));
  Multiplexer #(.select(5), .width(32)) multiplexer_1 (
    .in0(\n32位寄存器_1_q ), .in1(\n32位寄存器_9_q ), .in2(\n32位寄存器_17_q ), .in3(\n32位寄存器_25_q ),
    .in4(\n32位寄存器_2_q ), .in5(\n32位寄存器_10_q ), .in6(\n32位寄存器_18_q ), .in7(\n32位寄存器_26_q ),
    .in8(\n32位寄存器_3_q ), .in9(\n32位寄存器_11_q ), .in10(\n32位寄存器_19_q ), .in11(\n32位寄存器_27_q ),
    .in12(\n32位寄存器_4_q ), .in13(\n32位寄存器_12_q ), .in14(\n32位寄存器_20_q ), .in15(\n32位寄存器_28_q ),
    .in16(\n32位寄存器_5_q ), .in17(\n32位寄存器_13_q ), .in18(\n32位寄存器_21_q ), .in19(\n32位寄存器_29_q ),
    .in20(\n32位寄存器_6_q ), .in21(\n32位寄存器_14_q ), .in22(\n32位寄存器_22_q ), .in23(\n32位寄存器_30_q ),
    .in24(\n32位寄存器_7_q ), .in25(\n32位寄存器_15_q ), .in26(\n32位寄存器_23_q ), .in27(\n32位寄存器_31_q ),
    .in28(\n32位寄存器_8_q ), .in29(\n32位寄存器_16_q ), .in30(\n32位寄存器_24_q ), .in31(\n32位寄存器_32_q ), .out(rd2),
    .sel(ra2), .en(1'b1));
  Multiplexer #(.select(5), .width(32)) multiplexer_2 (
    .in0(\n32位寄存器_1_q ), .in1(\n32位寄存器_9_q ), .in2(\n32位寄存器_17_q ), .in3(\n32位寄存器_25_q ),
    .in4(\n32位寄存器_2_q ), .in5(\n32位寄存器_10_q ), .in6(\n32位寄存器_18_q ), .in7(\n32位寄存器_26_q ),
    .in8(\n32位寄存器_3_q ), .in9(\n32位寄存器_11_q ), .in10(\n32位寄存器_19_q ), .in11(\n32位寄存器_27_q ),
    .in12(\n32位寄存器_4_q ), .in13(\n32位寄存器_12_q ), .in14(\n32位寄存器_20_q ), .in15(\n32位寄存器_28_q ),
    .in16(\n32位寄存器_5_q ), .in17(\n32位寄存器_13_q ), .in18(\n32位寄存器_21_q ), .in19(\n32位寄存器_29_q ),
    .in20(\n32位寄存器_6_q ), .in21(\n32位寄存器_14_q ), .in22(\n32位寄存器_22_q ), .in23(\n32位寄存器_30_q ),
    .in24(\n32位寄存器_7_q ), .in25(\n32位寄存器_15_q ), .in26(\n32位寄存器_23_q ), .in27(\n32位寄存器_31_q ),
    .in28(\n32位寄存器_8_q ), .in29(\n32位寄存器_16_q ), .in30(\n32位寄存器_24_q ), .in31(\n32位寄存器_32_q ), .out(rd1),
    .sel(ra1), .en(1'b1));
  Multiplexer #(.select(5), .width(32)) multiplexer_3 (
    .in0(\n32位寄存器_1_q ), .in1(\n32位寄存器_9_q ), .in2(\n32位寄存器_17_q ), .in3(\n32位寄存器_25_q ),
    .in4(\n32位寄存器_2_q ), .in5(\n32位寄存器_10_q ), .in6(\n32位寄存器_18_q ), .in7(\n32位寄存器_26_q ),
    .in8(\n32位寄存器_3_q ), .in9(\n32位寄存器_11_q ), .in10(\n32位寄存器_19_q ), .in11(\n32位寄存器_27_q ),
    .in12(\n32位寄存器_4_q ), .in13(\n32位寄存器_12_q ), .in14(\n32位寄存器_20_q ), .in15(\n32位寄存器_28_q ),
    .in16(\n32位寄存器_5_q ), .in17(\n32位寄存器_13_q ), .in18(\n32位寄存器_21_q ), .in19(\n32位寄存器_29_q ),
    .in20(\n32位寄存器_6_q ), .in21(\n32位寄存器_14_q ), .in22(\n32位寄存器_22_q ), .in23(\n32位寄存器_30_q ),
    .in24(\n32位寄存器_7_q ), .in25(\n32位寄存器_15_q ), .in26(\n32位寄存器_23_q ), .in27(\n32位寄存器_31_q ),
    .in28(\n32位寄存器_8_q ), .in29(\n32位寄存器_16_q ), .in30(\n32位寄存器_24_q ), .in31(\n32位寄存器_32_q ), .out(rd0),
    .sel(ra0), .en(1'b1));
endmodule

module \_32位寄存器  (
  input  [31:0] D,
  input  en,
  input  clk,
  input  rst,
  output [31:0] Q
);

  Register #(.width(32)) register_1 (.D(D), .en(en), .Q(Q), .clk(clk), .clr(rst));
endmodule

module \_32位转16位  (
  input  [31:0] _32bits,
  output [15:0] _16bits
);


  assign _16bits = _32bits[15:0];
endmodule
